# Fritzing sketch CoinAcceptorWithDisplayAndMotors (saved by Fritzing 0.9.9b)

parts:
  U1 = ESP8266 NodeMCU LoLin module
  Mod1 = generic-ac-power-supply [package=THT]
  Part1 = Coin Acceptor - 6-Coin version
  R1 = Resistor [tolerance=±5% power=0.25 resistance=220 package=THT]
  LCD2004-I2C1 = LCD2004-I2C
  Arduino_CNC_Shield_V3_00_1 = Arduino_CNC_V3.00
  M1 = Stepper Motor - Bipolar  # not connected
  M2 = Stepper Motor - Bipolar
  M3 = Stepper Motor - Bipolar
  M4 = Stepper Motor - Bipolar  # not connected
  M5 = pcf8574 io expansion board [package=THT]
  M6 = pcf8574 io expansion board [package=THT]

nets:
  N1: U1.D1, LCD2004-I2C1.SCL, M5.SCL, M6.SCL
  N2: U1.D2, LCD2004-I2C1.SDA, M5.SDA, M6.SDA
  N3: U1.D3, Part1.SIG, R1.Pin_0
  N4: U1.3V3, R1.Pin_1
  GND: U1.GND, LCD2004-I2C1.GND, Arduino_CNC_Shield_V3_00_1.GND#2, M5.GND, M6.GND
  VCC: U1.Vin, LCD2004-I2C1.VCC, M5.VCC, M6.VCC
  N5: Mod1.pin3#2, Part1.12V, Arduino_CNC_Shield_V3_00_1.POWER_-
  N6: Mod1.pin3#3, Part1.GND, Arduino_CNC_Shield_V3_00_1.POWER_+
  N7: Arduino_CNC_Shield_V3_00_1.EN(able), M5.O4
  N8: Arduino_CNC_Shield_V3_00_1.X.STEP, M6.O0
  N9: Arduino_CNC_Shield_V3_00_1.X.DIR, M6.O1
  N10: Arduino_CNC_Shield_V3_00_1.Y.STEP, M6.O2
  N11: Arduino_CNC_Shield_V3_00_1.Y.DIR, M6.O3
  N12: Arduino_CNC_Shield_V3_00_1.Z.STEP, M6.O4
  N13: Arduino_CNC_Shield_V3_00_1.Z.DIR, M6.O5
  N14: Arduino_CNC_Shield_V3_00_1.A.STEP, M6.O6
  N15: Arduino_CNC_Shield_V3_00_1.A.DIR, M6.O7
  N16: Arduino_CNC_Shield_V3_00_1.X-MTR_'3', M3.C
  N17: Arduino_CNC_Shield_V3_00_1.Z-MTR_'2', M2.C
  N18: M5.A2+, M5.A2c
  N19: M5.A1+, M5.A1c
  N20: M5.A0+, M5.A0c
  N21: M6.A2c, M6.A2-
  N22: M6.A1+, M6.A1c
  N23: M6.A0+, M6.A0c

custom parts:
  ESP8266 NodeMCU LoLin module: ESP8266 based NodeMCU
  generic-ac-power-supply: Generic ac power supply module. Use as is, or customize the svgs to fit your particular device (as they are all different.) Provides AC input and single DC output. PCB is generic and will need modifications if you intend to do a pcb mount.
  Coin Acceptor - 6-Coin version: 12V coin acceptor that can handle up to 6 different denominations. Output is either pulse width, serial, or single pin per coin value.
  LCD2004-I2C: A standard character display with 4x20 characters. Comes in many colors with LCM2004 IIC attached.
  Arduino_CNC_V3.00: Protoneer Arduino CNC Shield V3.00 If using Grbl V0.9: The “A” axis can not be used (yet). The “SCL” (Arduino A5) pin is now used for 'Probing' input. The “End Stops Z+ & Z-” (Arduino D11) and “SpnEn” (Arduino D12) have been switched!
  pcf8574 io expansion board: pcf8574 io expansion board.
