# Fritzing sketch VM_v1.0 (saved by Fritzing 0.9.9b)

parts:
  U1 = ESP8266 NodeMCU LoLin module  # not connected
  LCD2 = LCD screen  # not connected
  LCM1602_IIC1 = LCM1602 IIC [part_number="LCM1602 IIC" chip_label="LCM1602 IIC" package="DIP (Dual Inline) [THT]"]
  U2 = PCF8574 [package="DIP16 [THT]"]
  U3 = PCF8574 [package="DIP16 [THT]"]  # not connected
  Arduino_CNC_Shield_V3_00_1 = Arduino_CNC_V3.00

nets:
  GND: LCM1602_IIC1.GND, U2.GND
  VCC: LCM1602_IIC1.VCC, U2.VCC
  N1: LCM1602_IIC1.SDA, U2.SDA
  N2: LCM1602_IIC1.SCL, U2.SCL
  N3: U2.P7, Arduino_CNC_Shield_V3_00_1.EN(able)

custom parts:
  ESP8266 NodeMCU LoLin module: ESP8266 based NodeMCU
  LCM1602 IIC: I2C-Module to use a 1602 or 2004 LCD on with the wire.h libory Serial LCD Modul
  Arduino_CNC_V3.00: Protoneer Arduino CNC Shield V3.00 If using Grbl V0.9: The “A” axis can not be used (yet). The “SCL” (Arduino A5) pin is now used for 'Probing' input. The “End Stops Z+ & Z-” (Arduino D11) and “SpnEn” (Arduino D12) have been switched!
