# Fritzing sketch CoinAcceptorWithDisplay (saved by Fritzing 0.9.9b)

parts:
  U1 = ESP8266 NodeMCU LoLin module
  Mod1 = generic-ac-power-supply [package=THT]
  Part1 = Coin Acceptor - 6-Coin version
  R1 = Resistor [tolerance=±5% power=0.25 resistance=220 package=THT]
  LCD2004-I2C1 = LCD2004-I2C

nets:
  N1: U1.D1, LCD2004-I2C1.SCL
  N2: U1.D2, LCD2004-I2C1.SDA
  N3: U1.D3, Part1.SIG, R1.Pin_0
  N4: U1.3V3, R1.Pin_1
  GND: U1.GND, LCD2004-I2C1.GND
  VIN: U1.Vin, LCD2004-I2C1.VCC
  N5: Mod1.pin3#2, Part1.12V
  N6: Mod1.pin3#3, Part1.GND

custom parts:
  ESP8266 NodeMCU LoLin module: ESP8266 based NodeMCU
  generic-ac-power-supply: Generic ac power supply module. Use as is, or customize the svgs to fit your particular device (as they are all different.) Provides AC input and single DC output. PCB is generic and will need modifications if you intend to do a pcb mount.
  Coin Acceptor - 6-Coin version: 12V coin acceptor that can handle up to 6 different denominations. Output is either pulse width, serial, or single pin per coin value.
  LCD2004-I2C: A standard character display with 4x20 characters. Comes in many colors with LCM2004 IIC attached.
