# Fritzing sketch ESP8266_RC522 (saved by Fritzing 0.9.9b)

parts:
  U1 = ESP8266 NodeMCU LoLin module
  Part1 = RFID-RC522-v2

nets:
  N1: U1.D3, Part1.RST
  3V3: U1.3V3, Part1.3.3V
  N2: U1.D5, Part1.SCK
  N3: U1.D6, Part1.MISO
  N4: U1.D7, Part1.MOSI
  N5: U1.D8, Part1.SDA
  GND: U1.GND, Part1.GND

custom parts:
  ESP8266 NodeMCU LoLin module: ESP8266 based NodeMCU
  RFID-RC522-v2: A simple China made RFID-RC522 Reader; do check the pin labels, as this is a MFRC522 based clone.
